# Fritzing sketch v0.01 (saved by Fritzing 0.9.2b)
circuit board: 15cm x 6cm
perfboards: 1

parts:
  元件1 = Arduino Uno (Rev3) [part_number="core board"]
  U1 = ESP8266-07 [part_number=ESP8266]
  元件2 = DHT11 [part_number=DT11]

nets:
  GND: 元件1.GND, U1.GND
  N1: 元件1.D0/RX, U1.TXD
  N2: 元件1.D1/TX, U1.RXD
  N3: 元件1.D2, 元件2.SIGNAL
  3V3: 元件1.3V3, U1.VCC
  N4: 元件1.5V, 元件2.VCC#2

custom parts:
  ESP8266-07: ESP8266 - 07 WiFi Module on PCB
  DHT11: The official support forum: support@iteadstudio.com
